// Logisim project counter_logic.circ as structural Verilog: 1 circuit, main circuit main
module main (
);

  wire and_1_out, clock_1_out, nand_1_out, nand_2_out, not_1_out, reset_count_out, start_count_out,
       stop_count_out;

  Clock clock_1 (.out(clock_1_out));
  Button start_count (.out(start_count_out));
  Button #(.press("passive")) stop_count (.out(stop_count_out));
  Button reset_count (.out(reset_count_out));
  not not_1 (not_1_out, start_count_out);
  nand nand_1 (nand_1_out, nand_2_out, stop_count_out);
  nand nand_2 (nand_2_out, not_1_out, nand_1_out);
  and and_1 (and_1_out, clock_1_out, nand_2_out);
  Counter counter_1 (.clr(reset_count_out), .clk(and_1_out));  // open: load, up, count, D, carry, Q
endmodule
